# Fritzing sketch Untitled Sketch (saved by Fritzing 1.0.1rc)
breadboards: 1

parts:
  Componente1 = Arduino Uno (Rev3)
  LCD1 = LCD screen
  R1 = Resistor [tolerance=±5% resistance=2000 package="0805 [SMD]"]
  LED1 = smd LED [color="Green (555nm)" package="0603 [SMD]"]
  LED2 = smd LED [color="Red (633nm)" package="0603 [SMD]"]
  R2 = Resistor [tolerance=±5% resistance=220 package="0805 [SMD]"]
  R3 = Resistor [tolerance=±5% resistance=220 package="0805 [SMD]"]
  HC-SR04_Sensor_1 = HC-SR04 Ultrasonic Distance Sensor
  S1 = Pushbutton [package="[SMD]"]
  Componente2 = Thumb Joystick
  RHT1 = Humidity and Temperature Sensor RHT03
  R5 = Resistor [tolerance=±5% resistance=10000 package="0805 [SMD]"]

nets:
  N1: Componente1.A1, Componente2.HORZ
  N2: Componente1.A2, Componente2.VERT
  N3: Componente1.A3, HC-SR04_Sensor_1.ECHO
  N4: Componente1.A4/SDA, HC-SR04_Sensor_1.TRIG
  N5: Componente1.A5/SCL, RHT1.Data-signal
  N6: Componente1.D8, LCD1.E
  N7: Componente1.D9_PWM, LCD1.RS
  N8: Componente1.D10_PWM/SS, LED1.anode
  N9: Componente1.D11_PWM/MOSI, LED2.anode
  N10: Componente1.D12/MISO, Componente2.SEL
  N11: Componente1.D2, S1.Pin_1, S1.Pin_2, R5.Pin_0
  N12: Componente1.D4, LCD1.DB7
  N13: Componente1.D5_PWM, LCD1.DB6
  N14: Componente1.D6_PWM, LCD1.DB5
  N15: Componente1.D7, LCD1.DB4
  VCC: Componente1.5V, LCD1.VDD, LCD1.LED+, HC-SR04_Sensor_1.VCC, Componente2.VCC, RHT1.Vcc
  GND: Componente1.GND, LCD1.VSS, LCD1.R/W, LCD1.LED-, R1.Pin_0, R2.Pin_1, R3.Pin_1, HC-SR04_Sensor_1.GND, Componente2.GND, RHT1.GND_2, R5.Pin_1
  N16: LCD1.V0, R1.Pin_1
  N17: LED1.cathode, R2.Pin_0
  N18: LED2.cathode, R3.Pin_0
  N19: S1.Pin_3, S1.Pin_4
